# Fritzing sketch PAM8403-sketch (saved by Fritzing 0.9.4)

parts:
  KT1 = SriKIT Mini FM Stereo Radio Module [part_number=KT0005 package=THT]
  AMP1 = GF1002 Stereo Amplifier
  SP1 = SPEAKER [package=pcb_mount_speaker]
  SP2 = SPEAKER [package=pcb_mount_speaker]

nets:
  N1: KT1.VCC, AMP1.POWER+
  N2: KT1.GND, AMP1.POWER-
  N3: KT1.AF-R, AMP1.INPUTL
  N4: KT1.AF-G, AMP1.INPUTG
  N5: KT1.AF-L, AMP1.INPUTR
  N6: AMP1.ROUT-, SP1.+
  N7: AMP1.ROUT+, SP1.-
  N8: AMP1.LOUT+, SP2.-
  N9: AMP1.LOUT-, SP2.+

notes:
  2 x 5W 8ohm Speaker
  PAM8403 Power Amplifier Module
  20cm - 30cm wire antenna
  +
  -
  Input from +5V DC Power Supply

custom parts:
  SriKIT Mini FM Stereo Radio Module: RDA5907M based FM stereo radio receiver module
  GF1002 Stereo Amplifier: GF1002 6 Watt Stereo Amplifier
